# Fritzing sketch Sketch (saved by Fritzing 0.9.3b)
circuit board: 8.46667cm x 5.64444cm
breadboards: 1

parts:
  Part1 = Arduino Nano (Rev3.0)
  Nokia_5110_LCD_Module1 = Nokia 5110 LCD
  J1 = Piezo Speaker
  LLC1 = Logic Level Converter [package="Breakout board"]
  R1 = Resistor [tolerance=±5% resistance=10k package="0603 [SMD]"]
  R2 = Resistor [tolerance=±5% resistance=330 package="0603 [SMD]"]
  KEYPAD1 = Membrane Matrix Keypad
  Part2 = HX711 Weighing Sensor Module
  R3 = Resistor [tolerance=±5% resistance=100 package="0402 [SMD]"]
  DS1 = DS18B20 1-Wire Temperature Sensor [part_number=DS18B20]
  R4 = Resistor [tolerance=±5% resistance=4.7 package="0402 [SMD]"]

nets:
  GND: Part1.GND, Nokia_5110_LCD_Module1.GND, Nokia_5110_LCD_Module1.GND_(out), J1.pin1, LLC1.L-GND, LLC1.H-GND, Part2.GND, DS1.GND
  N1: Part1.D2, KEYPAD1.7
  N2: Part1.D3, KEYPAD1.6
  N3: Part1.D4, KEYPAD1.5
  N4: Part1.D5, KEYPAD1.4
  N5: Part1.D6, KEYPAD1.3
  N6: Part1.D7, KEYPAD1.2
  N7: Part1.D8, KEYPAD1.1
  N8: Part1.D10, R4.Pin_1
  N9: Part1.D11/MOSI, Part2.CK/TX
  N10: Part1.D12/MISO, Part2.DO/RX
  5V: Part1.5V, LLC1.HV, Part2.VCC, DS1.VDD
  N11: Part1.A4, LLC1.HV4
  N12: Part1.A3, LLC1.HV3
  N13: Part1.A2, LLC1.HV2
  N14: Part1.A1, LLC1.HV1
  N15: Part1.A0, R3.Pin_1
  3V3: Part1.3V3, Nokia_5110_LCD_Module1.VCC, Nokia_5110_LCD_Module1.VCC_(out), LLC1.LV, R1.Pin_1, R2.Pin_1
  N16: Nokia_5110_LCD_Module1.SCE, Nokia_5110_LCD_Module1.SCE_(out), LLC1.LV4
  N17: Nokia_5110_LCD_Module1.RST, Nokia_5110_LCD_Module1.RST_(out), R1.Pin_0
  N18: Nokia_5110_LCD_Module1.D/C, Nokia_5110_LCD_Module1.D/C_(out), LLC1.LV3
  N19: Nokia_5110_LCD_Module1.DN(MOSI), Nokia_5110_LCD_Module1.DN(MODI)_(out), LLC1.LV2
  N20: Nokia_5110_LCD_Module1.SCLK, Nokia_5110_LCD_Module1.SCLK_(out), LLC1.LV1
  N21: Nokia_5110_LCD_Module1.LED, R2.Pin_0
  N22: J1.pin2, R3.Pin_0
  N23: DS1.DQ, R4.Pin_0

custom parts:
  Nokia 5110 LCD: Nokia 5110 Graphic 84*48 LCD module such as the Sparkfun LCD-10168 or the clones from Ebay. There is example code for the Arduino available from the Sparkfun site in https://learn.sparkfun.com/tutorials/graphic-lcd-hookup-guide This is a 3.3V device, if you are running it from a 5V micro you need a 5V tolorant level translator such as the 74ahc367 to protect the signal imputs. Rafa G. did a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
  Logic Level Converter: 5V to/from 3.3V logic level converter
  Membrane Matrix Keypad: Membrane Matrix 3x4 Keypad
